# Fritzing sketch Herisson v2 (saved by Fritzing 0.9.3b)
circuit board: 6.12249cm x 4.58152cm
breadboards: 1

parts:
  part = Adafruit HUZZAH ESP8266 [part_number=ESP8266]
  part_2 = Adafruit DS3231 [part_number=DS3231]
  LED3 = RGB LED (com. cathode, rbg) [package="5 mm [THT]"]
  R4 = Resistor [tolerance=±1% resistance=10k package=THT]
  S1 = Momentary Switch [package=ksa_sealed_tac_switch]
  R5 = Resistor [tolerance=±1% resistance=220 package=THT]
  R6 = Resistor [tolerance=±1% resistance=220 package=THT]
  R7 = Resistor [tolerance=±1% resistance=220 package=THT]
  R8 = PHOTOCELL [package=photocell-kit]
  R9 = Resistor [tolerance=±5% resistance=10k package=THT]
  R10 = Resistor [tolerance=±1% resistance=5.1k package=THT]
  R11 = Resistor [tolerance=±1% resistance=20k package=THT]
  JP1 = Header 2 [package=molex-1x2_lock]
  JP2 = Header 2 [package=molex-1x2_lock]
  JP3 = Header 2 [package=molex-1x2_lock]
  JP4 = Header 2 [package=molex-1x2_lock]
  JP5 = Header 2 [package=molex-1x2_lock]

nets:
  VIN: part.VIN, part_2.Vin, R11.Pin_0, JP4.2
  GND: part.GND, part_2.GND, LED3.common_cathode, R4.Pin_0, R9.Pin_0, R10.Pin_0, JP1.2, JP4.1
  N1: part.ADC, R8.P$1, R9.Pin_1, JP5.2
  N2: part.GPIO14, R5.Pin_1
  N3: part.GPIO12, R6.Pin_1
  N4: part.GPIO13, R7.Pin_1
  N5: part.3.3V, S1.3, JP3.2
  N6: part.GPIO15, R4.Pin_1, S1.2, JP3.1
  N7: part.GPIO4, part_2.SDA
  N8: part.GPIO5, part_2.SCL
  N9: LED3.red_anode, R5.Pin_0, JP1.1
  N10: LED3.blue_anode, R6.Pin_0, JP2.2
  N11: LED3.green_anode, R7.Pin_0, JP2.1
  N12: R8.P$2, R10.Pin_1, R11.Pin_1, JP5.1

custom parts:
  Adafruit HUZZAH ESP8266: Add Internet to your next project with an adorable, bite-sized WiFi microcontroller, at a price you like! The ESP8266 processor from Espressif is an 80 MHz microcontroller with a full WiFi front-end (both as client and access point) and TCP/IP stack with DNS support as well. While this chip has been very popular, its also been very difficult to use. Most of the low cost modules are not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
  Adafruit DS3231: The datasheet for the DS3231 explains that this part is an "Extremely Accurate I²C-Integrated RTC/TCXO/Crystal". And, hey, it does exactly what it says on the tin! This Real Time Clock (RTC) is the most precise you can get in a small, low power package. Most RTCs use an external 32kHz timing crystal that is used to keep time with low current draw. And that's all well and good, but those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
