# Fritzing sketch overview_V2 (saved by Fritzing 0.9.3b)
breadboards: 1

parts:
  Arduino_nano = Arduino Nano (Rev3.0)
  LED1 = RGB LED (com. cathode, rgb) [package="5 mm [THT]"]
  DS3231 = ZS-042 RTC Module
  Adafruit_HUZZAH_ESP8266_Breakout1 = Adafruit HUZZAH ESP8266 Breakout [part_number=2471]
  S1 = Pushbutton [package="[THT]"]
  R3 = Resistor [tolerance=±5% resistance=220 package=THT]
  IC1 = 24LC256 [package=THT]
  R4 = Resistor [tolerance=±5% resistance=220 package=THT]
  R6 = Resistor [tolerance=±5% resistance=220 package=THT]
  R5 = Resistor [tolerance=±5% resistance=220 package=THT]
  R2 = Resistor [tolerance=±5% resistance=10k package=THT]
  R1 = Photocell (LDR) [package=THT]

nets:
  N1: Arduino_nano.D1/TX, Adafruit_HUZZAH_ESP8266_Breakout1.RX
  N2: Arduino_nano.D0/RX, Adafruit_HUZZAH_ESP8266_Breakout1.TX
  GND: Arduino_nano.GND, LED1.common_cathode, DS3231.GND, Adafruit_HUZZAH_ESP8266_Breakout1.GND, S1.Pin_1, S1.Pin_2, IC1.A0, IC1.A1, IC1.A2, IC1.0V, IC1.WP_-_Write_Protect, R2.Pin_1
  N3: Arduino_nano.D3, R6.Pin_0
  N4: Arduino_nano.D5, R5.Pin_0
  N5: Arduino_nano.D6, R4.Pin_0
  N6: Arduino_nano.D10, S1.Pin_3, S1.Pin_4, R3.Pin_0
  5V: Arduino_nano.5V, DS3231.VCC, Adafruit_HUZZAH_ESP8266_Breakout1.VBat, R3.Pin_1, IC1.+V, R1.pin_0
  N7: Arduino_nano.A7, R2.Pin_0, R1.pin_1
  N8: Arduino_nano.A5, DS3231.SCL, IC1.SCL_-_I2C_Clock
  N9: Arduino_nano.A4, DS3231.SDA, IC1.SDA_-_I2C_Data
  N10: LED1.red_anode, R4.Pin_1
  N11: LED1.green_anode, R6.Pin_1
  N12: LED1.blue_anode, R5.Pin_1
